// Logisim project ejercicio1halfadder.circ as structural Verilog: 1 circuit, main circuit main
module main (
  input  A,
  input  B,
  output S,
  output C
);

  xor xor_1 (S, A, B);
  and and_1 (C, A, B);

  // Notes on the sheet:
  //   Ejercicio 1 – Semisumador (Half Adder) Crea un circuito con 2 entradas (A, B) que tenga 2 salidas: Suma (S) = A XOR B Acarreo (C) = A AND B
endmodule
