// Logisim project ejercicio2puertasnand.circ as structural Verilog: 1 circuit, main circuit main
module main (
  input  A,
  input  B,
  input  C,
  input  A1,
  input  B1,
  input  C1,
  input  D1,
  input  A2,
  output out_9,
  output out_10,
  output out_11
);

  wire nand_2_out, nand_3_out, nand_4_out;

  nand nand_1 (out_11, A2, A2);
  nand nand_2 (nand_2_out, A, B);
  nand nand_3 (nand_3_out, A1, B1);
  nand nand_4 (nand_4_out, C1, D1);
  nand nand_5 (out_9, nand_2_out, C);
  nand nand_6 (out_10, nand_3_out, nand_4_out);

  // Notes on the sheet:
  //   Puerta AND
  //   Puerta NAND universal Implementa una puerta AND, OR y NOT usando únicamente puertas NAND.
  //   Puerta OR
endmodule
